# Fritzing sketch IO (saved by Fritzing 0.9.4)
breadboards: 1

parts:
  Part1 = e-paper 2.9inch
  MCU1 = Raspberry Pi Zero
  Part2 = Arduino Uno (Rev3)
  Part3 = Ambient Light Sensor (TEMT6000 Breakout Board)
  U1 = POT [package=pot_mammoth]
  LED1 = LEDs [package=led10mm]

nets:
  N1: Part1.BUSY, Part1.GND, MCU1.pin_6, MCU1.pin_9, MCU1.pin_20
  N2: Part1.RST, MCU1.pin_21
  N3: Part1.DC, MCU1.pin_22
  N4: Part1.CS, MCU1.pin_24
  N5: Part1.CLK, MCU1.pin_23
  N6: Part1.DIN, MCU1.pin_19
  N7: Part1.VCC, MCU1.pin_1
  N8: Part2.A0, Part3.S
  N9: Part2.A1, U1.A
  N10: Part2.D13/SCK, LED1.A
  5V: Part2.5V, Part3.VCC, U1.S
  GND: Part2.GND, Part3.GND, U1.E, LED1.C
